# Fritzing sketch Smart-Sprayer (saved by Fritzing 0.9.3b)
breadboards: 1

parts:
  M1 = 1 chan 5v relay module
  M2 = 1 chan 5v relay module
  HC-SR04_Sensor_1 = HC-SR04 Ultrasonic Distance Sensor
  HC-SR04_Sensor_2 = HC-SR04 Ultrasonic Distance Sensor
  GSM_SIM_GPSR_SMS_SIM900_SIM1 = SIM800L [package=THT]
  C1 = Electrolytic Capacitor [capacitance=1000µF package="300 mil [THT, electrolytic]"]
  HLK-PM1 = HLK-PM12 [part_number=HLK-PM12]
  WATER_PUMP1 = water pump/motor
  WATER_PUMP2 = water pump/motor
  U2 = LM2596 step down module
  J1 = Piezo Speaker
  U5 = ESP32S-HiLetgo [part_number=ESP32S-HiLetgo]
  PCB2 = RTC_DS1302_module
  HLK-PM2 = HLK-PM12 [part_number=HLK-PM12]
  HLK-PM3 = HLK-PM12 [part_number=HLK-PM12]
  Raspberry_Pi_1 = Raspberry Pi 4 [part_number=RPI-4-b]  # not connected
  M3 = bb-usb-cable [package=THT]  # not connected

nets:
  VCC: M1.pin_1, M2.pin_1, HC-SR04_Sensor_1.VCC, HC-SR04_Sensor_2.VCC, GSM_SIM_GPSR_SMS_SIM900_SIM1.VDD, U2.OUT+, PCB2.VCC
  GND: M1.pin_2, M2.pin_2, HC-SR04_Sensor_1.GND, HC-SR04_Sensor_2.GND, GSM_SIM_GPSR_SMS_SIM900_SIM1.GND, C1.-, U2.IN-, U2.OUT-, PCB2.GND, HLK-PM3.-Vo
  N1: M1.pin_3, U5.GPIO21
  N2: M1.pin_4, WATER_PUMP2.pin_2
  N3: M1.pin_5, HLK-PM1.+Vo
  N4: M2.pin_3, U5.GPIO22
  N5: M2.pin_4, WATER_PUMP1.pin_2
  N6: M2.pin_5, HLK-PM2.+Vo
  N7: HC-SR04_Sensor_1.TRIG, U5.GPIO32
  N8: HC-SR04_Sensor_1.ECHO, U5.GPIO33
  N9: HC-SR04_Sensor_2.TRIG, U5.GPIO25
  N10: HC-SR04_Sensor_2.ECHO, U5.GPIO26
  N11: GSM_SIM_GPSR_SMS_SIM900_SIM1.5V, C1.+
  N12: GSM_SIM_GPSR_SMS_SIM900_SIM1.SIM_TXD, U5.GPIO4
  N13: GSM_SIM_GPSR_SMS_SIM900_SIM1.SIM_RXD, U5.GPIO16
  N14: HLK-PM1.-Vo, WATER_PUMP2.pin_1
  N15: WATER_PUMP1.pin_1, HLK-PM2.-Vo
  N16: U2.IN+, HLK-PM3.+Vo
  N17: J1.pin2, U5.GPIO23
  N18: U5.GPIO5, PCB2.DAT
  N19: U5.GPIO18, PCB2.CLK
  N20: U5.GPIO19, PCB2.RST

custom parts:
  1 chan 5v relay module: 1 Channel 5V Relay Module Board Shield with Optocoupler Support High and Low Level Trigger for Arduino.
  water pump/motor: WATER PUMP BY ARDUBLOCKTR
  LM2596 step down module: LM2596 DC-DC step down power supply module 3 A.
  ESP32S-HiLetgo: HiLetgo ESP-WROOM-32 ESP32 ESP-32S Development Board 2.4GHz Dual-Mode WiFi + Bluetooth Dual Cores Microcontroller The ESP32 integrated with Antenna switches, RF Balun, power amplifiers, low-noise amplifiers, filters, and management modules, and the entire solution occupies the least area of PCB. 2.4 GHz Wi-Fi plus Bluetooth dual-mode chip, with TSMC Ultra-low power consumption 40nm technology,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
  RTC_DS1302_module: Arduino module DS1302 SPI Real Time Clock
  Raspberry Pi 4: The RPi4, a faster version of the awesome Raspberry Pi 2 B ARM Board with 40 pin gpio. Ready for special Raspberry Pi B+ and RPi2 Hat (Hardware attached (on) top)
  bb-usb-cable: Breadboard only, no connectors USB cable for the Raspberry PIs.
