# Fritzing sketch Smart-Sprayer (saved by Fritzing 0.9.3b)
breadboards: 1

parts:
  U1 = ESP32S-HiLetgo [part_number=ESP32S-HiLetgo]
  M1 = 1 chan 5v relay module
  M2 = 1 chan 5v relay module
  HC-SR04_Sensor_1 = HC-SR04 Ultrasonic Distance Sensor
  HC-SR04_Sensor_2 = HC-SR04 Ultrasonic Distance Sensor
  U2 = LM2596 step down module
  LCD2004-I2C1 = LCD2004-I2C
  GSM_SIM_GPSR_SMS_SIM900_SIM1 = SIM800L [package=THT]
  C1 = Electrolytic Capacitor [capacitance=1000µF package="300 mil [THT, electrolytic]"]
  U4 = LM2596 step down module
  LED1 = LEDs [package=led10mm]
  ZS-042_RTC1 = ZS-042 RTC Module
  S1 = Round Pushbutton
  S2 = Round Pushbutton
  S3 = Round Pushbutton
  LED2 = LEDs [package=led10mm]
  S4 = Round Pushbutton
  J1 = Piezo Speaker
  HLK-PM1 = HLK-PM12 [part_number=HLK-PM12]
  WATER_PUMP1 = water pump/motor
  WATER_PUMP2 = water pump/motor

nets:
  N1: U1.GPIO32, LED2.A
  N2: U1.GPIO33, LED1.A
  N3: U1.GPIO25, S1.leg1
  N4: U1.GPIO26, S3.leg1
  N5: U1.GPIO27, S2.leg1
  N6: U1.GPIO14, HC-SR04_Sensor_2.ECHO
  N7: U1.GPIO12, HC-SR04_Sensor_2.TRIG
  N8: U1.GND, M1.pin_2, M2.pin_2, U2.IN-, U2.OUT-, LED1.C, S1.leg0, S2.leg0, S3.leg0, LED2.C, WATER_PUMP1.pin_1
  N9: U1.VIN, M1.pin_1, M2.pin_1, U2.OUT+
  N10: U1.GPIO0, J1.pin2
  N11: U1.GPIO4, M2.pin_3
  N12: U1.GPIO16, GSM_SIM_GPSR_SMS_SIM900_SIM1.SIM_TXD
  N13: U1.GPIO17, GSM_SIM_GPSR_SMS_SIM900_SIM1.SIM_RXD
  N14: U1.GPIO5, M1.pin_3
  N15: U1.GPIO18, HC-SR04_Sensor_1.ECHO
  N16: U1.GPIO19, HC-SR04_Sensor_1.TRIG
  N17: U1.GPIO21, LCD2004-I2C1.SDA, ZS-042_RTC1.SDA
  N18: U1.GPIO22, LCD2004-I2C1.SCL, ZS-042_RTC1.SCL
  N19: U1.GPIO23, S4.leg1
  N20: M1.pin_4, WATER_PUMP2.pin_2
  N21: M1.pin_5, M2.pin_5, U2.IN+, U4.IN+, HLK-PM1.+Vo
  N22: M2.pin_4, WATER_PUMP1.pin_2
  VCC: HC-SR04_Sensor_1.VCC, HC-SR04_Sensor_2.VCC, LCD2004-I2C1.VCC, ZS-042_RTC1.VCC
  GND: HC-SR04_Sensor_1.GND, HC-SR04_Sensor_2.GND, LCD2004-I2C1.GND, GSM_SIM_GPSR_SMS_SIM900_SIM1.GND#5, ZS-042_RTC1.GND, S4.leg0, J1.pin1
  5V: GSM_SIM_GPSR_SMS_SIM900_SIM1.5V, GSM_SIM_GPSR_SMS_SIM900_SIM1.VDD, C1.+, U4.OUT+
  N23: GSM_SIM_GPSR_SMS_SIM900_SIM1.GND#1, C1.-, U4.IN-, U4.OUT-, HLK-PM1.-Vo, WATER_PUMP2.pin_1

custom parts:
  ESP32S-HiLetgo: HiLetgo ESP-WROOM-32 ESP32 ESP-32S Development Board 2.4GHz Dual-Mode WiFi + Bluetooth Dual Cores Microcontroller The ESP32 integrated with Antenna switches, RF Balun, power amplifiers, low-noise amplifiers, filters, and management modules, and the entire solution occupies the least area of PCB. 2.4 GHz Wi-Fi plus Bluetooth dual-mode chip, with TSMC Ultra-low power consumption 40nm technology,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
  1 chan 5v relay module: 1 Channel 5V Relay Module Board Shield with Optocoupler Support High and Low Level Trigger for Arduino.
  LM2596 step down module: LM2596 DC-DC step down power supply module 3 A.
  LCD2004-I2C: A standard character display with 4x20 characters. Comes in many colors with LCM2004 IIC attached.
  water pump/motor: WATER PUMP BY ARDUBLOCKTR
